// Logisim project CO PROJECT.circ as structural Verilog: 3 circuits, main circuit MAIN
module MAIN (
  input  in_1,
  input  in_2,
  input  in_3,
  input  in_4,
  input  in_5,
  input  in_6,
  input  in_7,
  input  in_8,
  input  in_9,
  output [15:0] out_10,
  output [2:0] out_11
);

  wire CLK, INC_PC, LD_AC, LD_AR, LD_DR, LD_IR, LD_MEM, LD_PC;
  wire [2:0] ALU_Select;
  wire [6:0] AR, bit_extender_1_out, bit_extender_2_out, PC_q;
  wire [15:0] AC, ALU_output, bit_extender_3_out, bit_extender_4_out, DR_q, IR, ram_1_data, TR_q;

  Bit_Extender #(.in_width(16), .out_width(7)) bit_extender_1 (.in(out_10), .out(bit_extender_1_out));
  Bit_Extender #(.in_width(16), .out_width(7)) bit_extender_2 (.in(out_10), .out(bit_extender_2_out));
  Register #(.width(16)) u_AC (.D(ALU_output), .en(LD_AC), .Q(AC), .clk(CLK), .clr(in_4));
  Register #(.width(16)) DR (.D(out_10), .en(LD_DR), .Q(DR_q), .clk(CLK), .clr(in_5));
  Register #(.width(16)) TR (.D(out_10), .Q(TR_q), .clk(CLK), .clr(in_6));  // open: en
  Register #(.width(7)) u_AR (.D(bit_extender_1_out), .en(LD_AR), .Q(AR), .clk(CLK), .clr(in_7));
  Counter #(.width(7), .max('h7f)) PC (
    .load(LD_PC), .D(bit_extender_2_out), .count(INC_PC), .Q(PC_q), .clk(CLK), .clr(in_8));  // open: carry
  Register #(.width(16)) u_IR (.D(out_10), .en(LD_IR), .Q(IR), .clk(CLK), .clr(in_9));
  CU cu_1 (
    .IR(IR), .AR(AR), .AC(AC), .LD_IR(LD_IR), .LD_AR(LD_AR), .Bus_Select(out_11), .LD_AC(LD_AC),
    .LD_DR(LD_DR), .LD_MEM(LD_MEM), .ALU_Select(ALU_Select), .INC_PC(INC_PC), .LD_PC(LD_PC));  // open: out_6
  RAM #(.addrWidth(7), .dataWidth(16), .bus("separate")) ram_1 (
    .addr(AR), .din(out_10), .data(ram_1_data), .str(in_1), .sel(in_2), .clk(CLK), .ld(LD_MEM), .clr(in_3));
  ALU ALU (.A(DR_q), .B(AC), .Mux_In(ALU_Select), .Output(ALU_output));
  assign bit_extender_3_out = {{9{1'b0}}, AR};  // Bit_Extender bit_extender_3
  assign bit_extender_4_out = {{9{1'b0}}, PC_q};  // Bit_Extender bit_extender_4
  Multiplexer #(.select(3), .width(16), .enable("false")) multiplexer_1 (
    .in0(AC), .in1(DR_q), .in2(TR_q), .in3(bit_extender_3_out), .in4(ram_1_data), .in5(bit_extender_4_out),
    .in6(IR), .out(out_10), .sel(out_11));  // open: in7

  // Other names for the same wires on the sheet: Bus_Select[2:0] = out_11
endmodule

module ALU (
  input  [15:0] A,
  input  [15:0] B,
  input  [2:0] Mux_In,
  output [15:0] Output
);

  wire [15:0] adder_1_out, adder_2_out, and_1_out, multiplier_1_out, or_1_out, subtractor_1_out;

  Adder #(.width(16)) adder_1 (.a(A), .b(B), .out(adder_1_out));  // open: cin, cout
  Subtractor #(.width(16)) subtractor_1 (.a(A), .b(B), .out(subtractor_1_out));  // open: bin, bout
  Multiplier #(.width(16)) multiplier_1 (.a(A), .b(B), .out(multiplier_1_out));  // open: cin, cout
  Adder #(.width(16)) adder_2 (.a(A), .b(16'h1), .out(adder_2_out));  // open: cin, cout
  assign or_1_out = A | B;  // OR_Gate or_1, 16 bits wide
  assign and_1_out = A & B;  // AND_Gate and_1, 16 bits wide
  Multiplexer #(.select(3), .width(16), .enable("false")) multiplexer_1 (
    .in1(A), .in2(adder_1_out), .in3(subtractor_1_out), .in4(multiplier_1_out), .in5(adder_2_out),
    .in6(or_1_out), .in7(and_1_out), .out(Output), .sel(Mux_In));  // open: in0
endmodule

module CU (
  input  [15:0] IR,
  input  [6:0] AR,
  input  [15:0] AC,
  output LD_IR,
  output LD_AR,
  output out_6,
  output [2:0] Bus_Select,
  output LD_AC,
  output LD_DR,
  output LD_MEM,
  output [2:0] ALU_Select,
  output INC_PC,
  output LD_PC
);

  wire AC_Zero, AC_Zero_D6T5, CLR_SC, D0, D0T4, D0T5, D1, D1T4, D1T5, D2, D2T4, D2T5, D3, D3T4, D4, D5, D5T4,
       D5T5, D6, D6T4, D6T5, D6T6, D7, d_ff_1_q, INC, r, rB5, RD_AC, RD_MEM, T0, T2, T3, T4, T5, T6, T7, T8,
       T9, T10, T11, T12, T13, T14, T15;
  wire [3:0] SC_q;

  Clock Clk (.out(out_6));
  D_Flip_Flop d_ff_1 (.clk(out_6), .D(CLR_SC), .Q(d_ff_1_q));  // open: Qn, preset, en, reset
  Counter #(.width(4), .max('hf)) SC (.Q(SC_q), .clk(out_6), .clr(d_ff_1_q));  // open: load, D, count, carry
  Decoder #(.select(4)) decoder_1 (
    .out0(T0), .out1(LD_IR), .out2(T2), .out3(T3), .out4(T4), .out5(T5), .out6(T6), .out7(T7), .out8(T8),
    .out9(T9), .out10(T10), .out11(T11), .out12(T12), .out13(T13), .out14(T14), .out15(T15), .sel(SC_q));  // open: en
  or or_1 (CLR_SC, D2T5, D1T5, D0T5, LD_PC, D5T5, D3T4, D6T6, rB5);
  nor nor_1 (AC_Zero, AC[15], AC[14], AC[13], AC[12], AC[11], AC[10], AC[9], AC[8], AC[7], AC[6], AC[5], AC[4], AC[3], AC[2], AC[1], AC[0]);
  Decoder #(.select(3)) decoder_2 (
    .out0(D0), .out1(D1), .out2(D2), .out3(D3), .out4(D4), .out5(D5), .out6(D6), .out7(D7), .sel(IR[14:12]));  // open: en
  Priority_Encoder priority_encoder_1 (
    .in2(D1T5), .in3(D5T5), .in4(D0T5), .in5(INC), .out(ALU_Select));  // open: in0, in1, in6, in7, en_in, gs, en_out
  or or_2 (RD_AC, D6T5, rB5, D3T4);
  or or_3 (INC_PC, AC_Zero_D6T5, LD_IR);
  or or_4 (INC, D6T5, rB5);
  or or_5 (LD_AR, T0, T2);
  Priority_Encoder priority_encoder_2 (
    .in0(RD_AC), .in1(D2T5), .in3(LD_PC), .in4(RD_MEM), .in5(T0), .in6(T2), .out(Bus_Select));  // open: in2, in7, en_in, gs, en_out
  and and_1 (D2T4, D2, T4);
  and and_2 (D2T5, D2, T5);
  and and_3 (D0T4, D0, T4);
  and and_4 (D0T5, D0, T5);
  and and_5 (D1T4, D1, T4);
  and and_6 (D1T5, D1, T5);
  and and_7 (D3T4, D3, T4);
  and and_8 (r, D7, IR[15], T3);
  and and_9 (rB5, AR[5], r);
  or or_6 (RD_MEM, LD_IR, D2T4, D0T4, D1T4, D5T4, D6T4);
  or or_7 (LD_AC, D2T5, D0T5, D1T5, D5T5, D6T5, rB5);
  or or_8 (LD_DR, D2T4, D0T4, D1T4, D5T4, D6T4, rB5);
  or or_9 (LD_MEM, D3T4, D6T6);
  and and_10 (LD_PC, D4, T4);
  and and_11 (D5T4, D5, T4);
  and and_12 (D5T5, D5, T5);
  and and_13 (D6T4, D6, T4);
  and and_14 (D6T5, D6, T5);
  and and_15 (D6T6, D6, T6);
  and and_16 (AC_Zero_D6T5, AC_Zero, D6T6);

  // Other names for the same wires on the sheet: B5 = AR[5]; CLK = out_6; D4T4 = LD_PC; I_prime = IR[15]; T1 = LD_IR
endmodule
